# Fritzing sketch fritzing (saved by Fritzing 0.9.3b)
breadboards: 2

parts:
  S1 = H-Bridge with L298N
  J1 = Piezo Speaker
  Part1 = Arduino Nano (Rev3.0)
  Mod1 = Raspberry Pi 4B
  Mod2 = OLED Mono 0.56 inch blue or white
  U1 = RF-LINK_TX [package=rf-link_tx]
  VCC1 = 4 x AAA Battery Mount
  M1 = DC Motor
  M2 = DC Motor

nets:
  N1: S1.12V, VCC1.+
  GND: S1.GND, J1.pin1, Part1.GND, Mod1.GND, Mod2.GND, U1.GND
  N2: S1.ENA, Mod1.GPIO22
  N3: S1.IN1, Mod1.GPIO17
  N4: S1.IN2, Mod1.GPIO27
  N5: S1.IN3, Mod1.GPIO10
  N6: S1.IN4, Mod1.GPIO9
  N7: S1.ENB, Mod1.GPIO11
  N8: S1.M1-01, M1.pin_2
  N9: S1.M1-02, M1.pin_1
  N10: S1.M2-01, M2.pin_1
  N11: S1.M2-02, M2.pin_2
  N12: J1.pin2, Part1.D10
  N13: Part1.D11/MOSI, U1.DATA
  N14: Part1.D12/MISO, U1.+5V
  VIN: Part1.VIN, Mod1.5V
  5V: Part1.5V, Mod2.VCC, U1.ANT
  N15: Part1.A5, Mod2.SCL
  N16: Part1.A4, Mod2.SDA

notes:
  DFRobot Serial 6-Axis Accelerometer

custom parts:
  H-Bridge with L298N: h-bridge
  OLED Mono 0.56 inch blue or white: OLED, I2C 3.3V - 5V Blue and White text versions
